# Fritzing sketch eighties_arp (saved by Fritzing 0.9.10b)
breadboards: 1

parts:
  Part1 = Adafruit QT Py RP2040 [part_number="Adafruit #4900"]
  Part2 = TRRS 3.5mm Jack Breakout
  R1 = Resistor [tolerance=±5% power=0.25 resistance=1k package=THT]
  C1 = Ceramic Capacitor [capacitance=100nF voltage=35V package="100 mil [THT, multilayer]"]
  R2 = Rotary Potentiometer (Small) [maximum_resistance=100kΩ knob_status=50% power=0.5W package=THT]
  R3 = Rotary Potentiometer (Small) [maximum_resistance=100kΩ knob_status=50% power=0.5W package=THT]
  S1 = Pushbutton [package="[THT]"]
  S2 = Pushbutton [package="[THT]"]

nets:
  GND: Part1.GND, Part2.SLEEVE, C1.1, R2.leg1, R3.leg1, S1.Pin_3, S1.Pin_4, S2.Pin_3, S2.Pin_4
  N1: Part1.A0, R2.wiper
  N2: Part1.A1, R3.wiper
  N3: Part1.SDA, S1.Pin_1, S1.Pin_2
  N4: Part1.SCL, S2.Pin_1, S2.Pin_2
  N5: Part1.RX, R1.Pin_0
  5V: Part1.+3V3, R2.leg2, R3.leg2
  N6: Part2.RING1, Part2.TIP, R1.Pin_1, C1.0

custom parts:
  Adafruit QT Py RP2040: Description What a cutie pie! Or is it... a QT Py? This diminutive dev board comes with one of our new favorite chip, the RP2040. It's been made famous in the new Raspberry Pi Pico and our Feather RP2040 and ItsyBitsy RP2040, but what if we wanted something really smol? A new chip means a new QT Py, and the Raspberry Pi RP2040 is no exception. When we saw this chip we thought "this chip is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
