# Fritzing sketch monosynth1 (saved by Fritzing 0.9.10b)
breadboards: 1

parts:
  Part1 = Adafruit QT Py RP2040 [part_number="Adafruit #4900"]
  Audio_Out = TRRS 3.5mm Jack Breakout
  R1 = Resistor [tolerance=±5% power=0.25 resistance=1k package=THT]
  C1 = Ceramic Capacitor [capacitance=100nF voltage=35V package="100 mil [THT, multilayer]"]
  MIDI_TRS-A = TRRS 3.5mm Jack Breakout
  IC1 = IC, DIP package, 8 pins [chip_label=6N138]
  R5 = Resistor [tolerance=±5% power=0.25 resistance=4.7k package=THT]
  R6 = Resistor [tolerance=±5% power=0.25 resistance=220 package=THT]
  D1 = Rectifier Diode [part_number=1N4001 package="300 mil [THT]"]
  R7 = Resistor [tolerance=±5% power=0.25 resistance=470 package=THT]

nets:
  GND: Part1.GND, Audio_Out.SLEEVE, C1.1, IC1.pin5, R5.Pin_1
  N1: Part1.RX, IC1.pin6, R7.Pin_1
  N2: Part1.SCK, R1.Pin_0
  5V: Part1.+3V3, R7.Pin_0
  N3: Audio_Out.RING1, Audio_Out.TIP, R1.Pin_1, C1.0
  N4: MIDI_TRS-A.RING1, R6.Pin_1, D1.cathode
  N5: MIDI_TRS-A.TIP, IC1.pin3, D1.anode
  N6: IC1.pin2, R6.Pin_0
  N7: IC1.pin7, R5.Pin_0

notes:
  note: 6N138 not guaranteed to work at 3.3V

custom parts:
  Adafruit QT Py RP2040: Description What a cutie pie! Or is it... a QT Py? This diminutive dev board comes with one of our new favorite chip, the RP2040. It's been made famous in the new Raspberry Pi Pico and our Feather RP2040 and ItsyBitsy RP2040, but what if we wanted something really smol? A new chip means a new QT Py, and the Raspberry Pi RP2040 is no exception. When we saw this chip we thought "this chip is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
