# Fritzing sketch synthio_pico_i2s (saved by Fritzing 0.9.10b)
breadboards: 1

parts:
  Pico = Raspberry Pi Pico
  PCM5102A_I2S_Stereo_DAC3 = PCM5102A I2S Stereo DAC tod

nets:
  N1: Pico.pin_3, Pico.pin_8, Pico.pin_13, Pico.pin_18, Pico.pin_23, Pico.pin_28, Pico.pin_33, Pico.pin_38, Pico.pin_42, PCM5102A_I2S_Stereo_DAC3.SCK, PCM5102A_I2S_Stereo_DAC3.GND
  N2: Pico.pin_15, PCM5102A_I2S_Stereo_DAC3.BCK
  N3: Pico.pin_16, PCM5102A_I2S_Stereo_DAC3.LRCK
  N4: Pico.pin_36, PCM5102A_I2S_Stereo_DAC3.VIN

custom parts:
  Raspberry Pi Pico: Raspberry Pi Pico. Based around the RP2040 microcontroller the Pico is a low cost microcontroller device bringing Raspberry Pi quality, cost, and easy of use to the microcontroller space. Jan 2021, Split part in to two versions: tht (this one) and SMD. This one will drill holes for a .1 in header in pcb to allow plugging in the module as well as providing pads to solder the module to the top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
  PCM5102A I2S Stereo DAC tod: PCM5102A I2S Stereo DAC
